# Fritzing sketch circuit (saved by Fritzing 0.9.3b)
breadboards: 1

parts:
  Part1 = Adafruit DRV8833 DC/Stepper Motor Driver [part_number="Adafruit #3297"]
  Part2 = Adafruit DRV8833 DC/Stepper Motor Driver [part_number="Adafruit #3297"]
  Q1 = NPN-Transistor [package="TO92 [THT]"]
  M1 = DC Motor  # not connected
  R1 = Resistor [tolerance=±5% resistance=220 package=THT]
  D1 = Rectifier Diode [part_number=1N4001 package="300 mil [THT]"]
  Part3 = Arduino Uno (Rev3)
  VCC1 = Battery
  VCC2 = Battery
  VCC3 = Battery
  M2 = Stepper Motor - Bipolar
  M3 = Stepper Motor - Bipolar

nets:
  N1: Part1.PWRIN, Part2.NFAULT
  GND: Part1.GND, Part2.GND, Q1.E, Part3.GND
  N2: Part1.AOUT2, M2.C
  N3: Part1.AOUT1, M2.A
  N4: Part1.BOUT1, M2.D
  N5: Part1.BOUT2, M2.B
  N6: Part1.BIN1, Part3.D8
  N7: Part1.BIN2, Part3.D4
  N8: Part1.!SLEEP, Part2.!SLEEP, Part3.5V
  N9: Part2.PWRIN, D1.cathode
  N10: Part2.AOUT2, Part3.D10_PWM/SS, M3.C
  N11: Part2.AIN2, Part3.D7
  N12: Part2.AIN1, Part3.D6_PWM
  N13: Q1.B, D1.anode
  N14: Q1.C, R1.Pin_1
  N15: Part3.VIN, VCC1.+
  N16: VCC1.-, VCC3.+
  N17: VCC2.+, VCC3.-

custom parts:
  Adafruit DRV8833 DC/Stepper Motor Driver: Spin two DC motors or step one bi-polar or uni-polar stepper with up to 1.2A per channel using the DRV8833. This motor driver chip is a nice alternative to the TB6612 driver. Like that chip, you get 2 full H-bridges, but this chip is better for low voltage uses (can run from 2.7V up to 10.8V motor power) and has built in current limiting capability. We set it up for 1A current limiting so you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
